# Fritzing sketch Pixel-Ring-Trinket-Clock (saved by Fritzing 0.8.5b)
breadboards: 1

parts:
  RTC1 = DS1307 RTC Breakout
  neopixel1 = Neopixel Ring 16
  TRINKET1 = Trinket 5V

nets:
  GND: RTC1.GND, neopixel1.GND, TRINKET1.no_name_yet#2
  5V: RTC1.5V, neopixel1.VCC, TRINKET1.no_name_yet#6
  N1: RTC1.SDA, TRINKET1.no_name_yet#9
  N2: RTC1.SCL, TRINKET1.no_name_yet#7
  N3: neopixel1.IN, TRINKET1.no_name_yet#8

custom parts:
  DS1307 RTC Breakout: DS1307 Real-time Clock Breakout Board with Battery
  Neopixel Ring 16: Neopixel Ring x16
  Trinket 5V: Adafruit Trinket 5V
